// Logisim project simple_processor.circ as structural Verilog: 7 circuits, main circuit main
module main (
);

  wire clk, rst;
  wire [2:0] addr0, addr1, ALU_OP;
  wire [7:0] program_counter_q, reg_group_a, reg_group_b, val;
  wire [16:0] rom_1_data;

  Button start ();  // open: out
  Button u_clk (.out(clk));
  Button reset (.out(rst));
  // Probe on program_counter_q
  program_counter program_counter (.count(clk), .clk(clk), .reset(rst), .Q(program_counter_q));  // open: load, D
  ROM #(.dataWidth(17)) rom_1 (.addr(program_counter_q), .data(rom_1_data));  // open: sel
  // Probe on rom_1_data
  ctrl ctrl (.instruction(rom_1_data), .opcode(ALU_OP), .Addr0(addr0), .Addr1(addr1), .val(val));
  ALU ALU (.en(clk), .OP(ALU_OP), .D0(reg_group_a), .D1(reg_group_b));  // open: Q
  bus instruction_bus ();  // open: D_en, in, D, out
  cache cache (.clk(clk), .reset(rst));  // open: in, ld, addr, out
  registers reg_0_7 (
    .clk(clk), .reset(rst), .D(val), .sel(addr0), .reg_0(reg_group_a), .reg_1(reg_group_a),
    .reg_2(reg_group_a), .reg_3(reg_group_a), .reg_4(reg_group_a), .reg_5(reg_group_a), .reg_6(reg_group_a),
    .reg_7(reg_group_a));
  registers reg_8_13 (
    .clk(clk), .reset(rst), .D(val), .sel(addr1), .reg_0(reg_group_b), .reg_1(reg_group_b),
    .reg_2(reg_group_b), .reg_3(reg_group_b), .reg_4(reg_group_b), .reg_5(reg_group_b), .reg_6(reg_group_b),
    .reg_7(reg_group_b));
  bus mem_bus ();  // open: D_en, in, D, out

  // Notes on the sheet:
  //   contents of rom_1 (hex, n*v repeats v):
  //   12 2 31
endmodule

module program_counter (
  input  load,
  input  [7:0] D,
  input  count,
  input  clk,
  input  reset,
  output [7:0] Q
);

  Counter counter_1 (.load(load), .D(D), .count(count), .Q(Q), .clk(clk), .clr(reset));  // open: carry
endmodule

module bus (
  input  D_en,
  input  [7:0] D,
  input  [7:0] in,
  output [7:0] out
);

  // Transmission_Gate #(.width(8)) transmission_1: pin names not known; wires that end beside it: D_en, D, in, D_en

  assign out = in;

  // Other names for the same wires on the sheet: Data_Ctrl = D_en
endmodule

module ALU (
  input  en,
  input  [2:0] OP,
  input  [7:0] D0,
  input  [7:0] D1,
  output [7:0] Q
);

  wire [7:0] adder_1_out, divider_1_out, multiplier_1_out, subtractor_1_out;

  Adder adder_1 (.a(D0), .b(D1), .out(adder_1_out));  // open: cin, cout
  Subtractor subtractor_1 (.a(D0), .b(D1), .out(subtractor_1_out));  // open: bin, bout
  Multiplier multiplier_1 (.a(D0), .b(D1), .out(multiplier_1_out));  // open: cin, cout
  Divider divider_1 (.a(D0), .b(D1), .out(divider_1_out));  // open: upper, rem
  BitAdder bitadder_1 ();  // open: in0, out
  Negator negator_1 ();  // open: in, out
  Comparator comparator_1 ();  // open: a, b, gt, eq, lt
  Shifter shifter_1 ();  // open: in, dist, out
  Multiplexer #(.select(3), .width(8)) multiplexer_1 (
    .in0({8{1'b0}}), .in1(8'h1), .in2(adder_1_out), .in3(subtractor_1_out), .in4(multiplier_1_out),
    .in5(divider_1_out), .out(Q), .sel(OP), .en(en));  // open: in6, in7
endmodule

module registers (
  input  clk,
  input  reset,
  input  [7:0] D,
  input  [2:0] sel,
  output [7:0] reg_0,
  output [7:0] reg_1,
  output [7:0] reg_2,
  output [7:0] reg_3,
  output [7:0] reg_4,
  output [7:0] reg_5,
  output [7:0] reg_6,
  output [7:0] reg_7
);

  wire Reg_0_t, Reg_1_t, Reg_2_t, Reg_3_t, Reg_4_t, Reg_5_t, Reg_6_t, Reg_7_t;

  Decoder #(.select(3), .enable("false")) decoder_1 (
    .out0(Reg_0_t), .out1(Reg_1_t), .out2(Reg_2_t), .out3(Reg_3_t), .out4(Reg_4_t), .out5(Reg_5_t),
    .out6(Reg_6_t), .out7(Reg_7_t), .sel(sel));
  Register u_Reg_0 (.D(D), .en(Reg_0_t), .Q(reg_0), .clk(clk), .clr(reset));
  Register u_Reg_2 (.D(D), .en(Reg_2_t), .Q(reg_2), .clk(clk), .clr(reset));
  Register u_Reg_4 (.D(D), .en(Reg_4_t), .Q(reg_4), .clk(clk), .clr(reset));
  Register u_Reg_6 (.D(D), .en(Reg_6_t), .Q(reg_6), .clk(clk), .clr(reset));
  Register u_Reg_1 (.D(D), .en(Reg_1_t), .Q(reg_1), .clk(clk), .clr(reset));
  Register u_Reg_3 (.D(D), .en(Reg_3_t), .Q(reg_3), .clk(clk), .clr(reset));
  Register u_Reg_5 (.D(D), .en(Reg_5_t), .Q(reg_5), .clk(clk), .clr(reset));
  Register u_Reg_7 (.D(D), .en(Reg_7_t), .Q(reg_7), .clk(clk), .clr(reset));

  // Other names for the same wires on the sheet: Data[7:0] = D; rst = reset
endmodule

module cache (
  input  [7:0] in,
  input  ld,
  input  [7:0] addr,
  input  clk,
  input  reset,
  output [7:0] out
);

  wire not_1_out;

  assign out = ld ? in : 8'bz;  // Controlled_Buffer controlled_buffer_1
  not not_1 (not_1_out, ld);
  RAM ram_1 (.addr(addr), .data(out), .clk(clk), .ld(not_1_out), .clr(reset));  // open: sel

  // Notes on the sheet:
  //   Reference: Logisim library documentation
endmodule

module ctrl (
  input  [16:0] instruction,
  output [2:0] opcode,
  output [2:0] Addr0,
  output [2:0] Addr1,
  output [7:0] val
);


  assign Addr0 = instruction[5:3];
  assign Addr1 = instruction[8:6];
  assign opcode = instruction[2:0];
  assign val = instruction[16:9];
endmodule
